# Fritzing sketch Untitled Sketch (saved by Fritzing 0.9.3b)
breadboards: 1

parts:
  Raspberry_Pi_1 = Raspberry Pi 3 [part_number=RPI-3-V1.2]
  LED1 = smd LED [color="Yellow (574nm)" package="0805 [SMD]"]
  LED2 = smd LED [color="Red (633nm)" package="0805 [SMD]"]
  LED3 = smd LED [color="Yellow (595nm)" package="0805 [SMD]"]
  R1 = Resistor [tolerance=±5% resistance=220 package=THT]
  LED4 = smd LED [color="Red (633nm)" package="0805 [SMD]"]
  LED5 = smd LED [color="Yellow (595nm)" package="0805 [SMD]"]
  LED6 = smd LED [color="Yellow (595nm)" package="0805 [SMD]"]
  LED7 = smd LED [color="Yellow (574nm)" package="0805 [SMD]"]
  LED8 = smd LED [color="Yellow (574nm)" package="0805 [SMD]"]
  LCD1 = LCD screen  # not connected
  R2 = Resistor [tolerance=±5% resistance=220 package=THT]
  R3 = Resistor [tolerance=±5% resistance=220 package=THT]
  R4 = Resistor [tolerance=±5% resistance=220 package=THT]
  R5 = Resistor [tolerance=±5% resistance=220 package=THT]
  R6 = Resistor [tolerance=±5% resistance=220 package=THT]
  R7 = Resistor [tolerance=±5% resistance=220 package=THT]
  R8 = Resistor [tolerance=±5% resistance=220 package=THT]

nets:
  N1: Raspberry_Pi_1.GND, LED1.cathode, LED2.cathode, LED3.cathode, LED4.cathode, LED5.cathode, LED6.cathode, LED7.cathode, LED8.cathode
  N2: Raspberry_Pi_1.GIPO17, R8.Pin_1
  N3: Raspberry_Pi_1.GIPO27, R7.Pin_1
  N4: Raspberry_Pi_1.GIPO11, R5.Pin_1
  N5: Raspberry_Pi_1.GIPO5, R6.Pin_1
  N6: Raspberry_Pi_1.GIPO6, R4.Pin_1
  N7: Raspberry_Pi_1.GIPO13, R3.Pin_1
  N8: Raspberry_Pi_1.GIPO19, R2.Pin_1
  N9: Raspberry_Pi_1.GIPO26, R1.Pin_1
  N10: LED1.anode, R8.Pin_0
  N11: LED2.anode, R6.Pin_0
  N12: R1.Pin_0, LED8.anode
  N13: LED4.anode, R5.Pin_0
  N14: LED5.anode, R4.Pin_0
  N15: LED6.anode, R7.Pin_0
  N16: LED7.anode, R2.Pin_0
